# Fritzing sketch StairLights (saved by Fritzing 0.9.3b)

parts:
  U1 = NodeMCU V1.0
  V1 = DC Power [voltage=5]
  NEOPIXEL2 = Neopixel Strip -- Black (30/m)
  PIR1 = PIR sensor
  PIR2 = PIR sensor
  NEOPIXEL3 = Neopixel Strip -- Black (30/m)
  R1 = Resistor [tolerance=±5% resistance=220 package=THT]
  C2 = Electrolytic Capacitor [capacitance=1000μF package="1010 [SMD, electrolytic]"]

nets (from the schematic view):
  N1: U1.D0, R1.Pin_1
  N2: U1.D1, PIR1.SIG
  N3: U1.D2, PIR2.SIG
  VIN: U1.Vin, V1.V+, NEOPIXEL2.+5V#1, PIR1.VDD, NEOPIXEL3.+5V#6, C2.+
  GND: V1.V-, PIR1.GND, PIR2.GND, NEOPIXEL3.GND#4
  N4: NEOPIXEL2.DI, R1.Pin_0
  N5: NEOPIXEL2.GND#3, C2.-
  N6: NEOPIXEL2.GND#4, NEOPIXEL3.GND#3
  N7: NEOPIXEL2.DO, NEOPIXEL3.DI
  N8: NEOPIXEL2.+5V#6, NEOPIXEL3.+5V#1

custom parts:
  NodeMCU V1.0: ESP8266 based NodeMCU
  Neopixel Strip -- Black (30/m): Neopixel Strip, Black, 30 pixels per meter.
